// Logisim project cpu.circ as structural Verilog: 11 circuits, main circuit main_8bit
module main_4bit (
);

  wire and_1_out, and_2_out, and_3_out, and_4_out, and_5_out, and_6_out, and_7_out, and_8_out, and_9_out,
       and_10_out, and_11_out, button_1_out, button_2_out, button_3_out, button_4_out, button_5_out,
       button_6_out, button_7_out, button_8_out, button_10_out, button_11_out, clock_1_out, d_ff_1_qn,
       d_ff_2_q, d_ff_3_q, d_ff_4_q, decoder_1_out0, decoder_1_out1, decoder_2_out0, decoder_2_out1,
       decoder_3_out0, decoder_3_out2, decoder_3_out3, decoder_3_out7, decoder_4_out0, decoder_5_out0,
       decoder_5_out1, decoder_5_out2, digital_oscilloscope_1_p2, n7_segment_display_2_p1,
       n7_segment_display_2_p2, nor_1_out, not_1_out, or_1_out, or_2_out, or_3_out, or_4_out, or_5_out,
       or_6_out, or_7_out, or_8_out, or_9_out, or_10_out, or_11_out, pull_resistor_1_node,
       pull_resistor_4_node, switch_2_p2, switch_2_p3, xor_1_out;
  wire [1:0] counter_2_q;
  wire [3:0] add_sub_4bit_1_c0, alu_4bit_1_c0, alu_4bit_1_zf, controlled_buffer_1_out,
       controlled_buffer_2_out, controlled_buffer_3_out, counter_1_q, dipswitch_1_p4, latch_8bit_1_q0,
       pull_resistor_2_node, register_3_q;
  wire [7:0] AX_q, BX_q, register_1_q, register_2_q, rom_1_data;

  // DipSwitch #(.number(4)) dipswitch_1: pin names not known; wires that end beside it: dipswitch_1_p4[3], dipswitch_1_p4[2], dipswitch_1_p4[1], dipswitch_1_p4[0]
  assign controlled_buffer_1_out = pull_resistor_1_node ? dipswitch_1_p4 : 4'bz;  // Controlled_Buffer controlled_buffer_1
  Pull_Resistor pull_resistor_1 (.node(pull_resistor_1_node));
  // Switch switch_1: pin names not known; wires that end beside it: pull_resistor_1_node, 1'b1
  Pull_Resistor pull_resistor_2 (.node(pull_resistor_2_node));
  buf or_1 (or_1_out, and_3_out);  // OR_Gate
  Button button_1 (.out(button_1_out));
  Button button_2 (.out(button_2_out));
  Decoder #(.select(4)) decoder_1 (
    .out0(decoder_1_out0), .out1(decoder_1_out1), .sel(register_2_q[7:4]), .en(or_1_out));  // open: out2, out3, out4, out5, out6, out7, out8, out9, out10, out11, out12, out13, out14, out15
  Decoder #(.select(4)) decoder_2 (
    .out0(decoder_2_out0), .out1(decoder_2_out1), .sel(register_2_q[3:0]), .en(or_1_out));  // open: out2, out3, out4, out5, out6, out7, out8, out9, out10, out11, out12, out13, out14, out15
  Register #(.trigger("high")) AX (
    .D({pull_resistor_2_node, controlled_buffer_1_out}), .clk(or_2_out), .Q(AX_q), .clr(button_3_out));  // open: en
  Button button_3 (.out(button_3_out));
  or or_2 (or_2_out, button_1_out, xor_1_out);
  Register #(.trigger("high")) BX (
    .D({pull_resistor_2_node, controlled_buffer_1_out}), .clk(button_2_out), .Q(BX_q), .clr(button_4_out));  // open: en
  Button button_4 (.out(button_4_out));
  Decoder #(.select(4)) decoder_3 (
    .out0(decoder_3_out0), .out2(decoder_3_out2), .out3(decoder_3_out3), .out7(decoder_3_out7),
    .sel(register_1_q[7:4]));  // open: out1, out4, out5, out6, out8, out9, out10, out11, out12, out13, out14, out15, en
  Decoder #(.select(4)) decoder_4 (
    .out0(decoder_4_out0), .sel(register_1_q[3:0]));  // open: out1, out2, out3, out4, out5, out6, out7, out8, out9, out10, out11, out12, out13, out14, out15, en
  or or_3 (or_3_out, decoder_3_out3, decoder_3_out7, decoder_3_out2);
  assign controlled_buffer_2_out = decoder_2_out0 ? AX_q[3:0] : 4'bz;  // Controlled_Buffer controlled_buffer_2
  assign controlled_buffer_3_out = decoder_1_out0 ? AX_q[3:0] : 4'bz;  // Controlled_Buffer controlled_buffer_3
  assign controlled_buffer_2_out = decoder_2_out1 ? BX_q[3:0] : 4'bz;  // Controlled_Buffer controlled_buffer_4
  assign controlled_buffer_3_out = decoder_1_out1 ? BX_q[3:0] : 4'bz;  // Controlled_Buffer controlled_buffer_5
  and and_1 (and_1_out, decoder_3_out0, nor_1_out);
  or or_4 (or_4_out, decoder_3_out3, decoder_3_out7, decoder_3_out2);
  and and_2 (and_2_out, decoder_4_out0, or_4_out);
  and and_3 (and_3_out, decoder_5_out1, and_2_out);
  ALU_4bit alu_4bit_1 (
    .Enable(or_3_out), .Latch(or_7_out), .A0(controlled_buffer_3_out[0]), .A1(controlled_buffer_3_out[1]),
    .A2(controlled_buffer_3_out[2]), .A3(controlled_buffer_3_out[3]), .B0(controlled_buffer_2_out[0]),
    .B1(controlled_buffer_2_out[1]), .B3(controlled_buffer_2_out[2]), .B4(controlled_buffer_2_out[3]),
    .Sign(decoder_3_out3), .Reset(or_8_out), .in_1(register_1_q[7:4]), .C0(alu_4bit_1_c0[0]),
    .C1(alu_4bit_1_c0[1]), .C2(alu_4bit_1_c0[2]), .C3(alu_4bit_1_c0[3]), .ZF(alu_4bit_1_zf[0]),
    .CF(alu_4bit_1_zf[1]), .OFlag(alu_4bit_1_zf[2]), .SF(alu_4bit_1_zf[3]));  // open: Cin
  ROM #(.addrWidth(4)) rom_1 (.addr(counter_1_q), .data(rom_1_data));
  Decoder #(.select(2)) decoder_5 (
    .out0(decoder_5_out0), .out1(decoder_5_out1), .out2(decoder_5_out2), .sel(counter_2_q));  // open: out3, en
  and and_4 (and_4_out, and_2_out, decoder_5_out2);
  buf or_5 (or_5_out, and_3_out);  // OR_Gate
  buf or_6 (or_6_out, and_4_out);  // OR_Gate
  buf or_7 (or_7_out, and_3_out);  // OR_Gate
  assign controlled_buffer_1_out = xor_1_out ? alu_4bit_1_c0 : 4'bz;  // Controlled_Buffer controlled_buffer_6
  or or_8 (or_8_out, button_5_out, d_ff_3_q);
  Button button_5 (.out(button_5_out));
  Register #(.trigger("high")) register_1 (.D(rom_1_data), .clk(decoder_5_out0), .Q(register_1_q));  // open: en, clr
  Register #(.trigger("high")) register_2 (
    .D(rom_1_data), .clk(decoder_5_out1), .Q(register_2_q), .clr(button_6_out));  // open: en
  buf or_9 (or_9_out, and_1_out);  // OR_Gate
  Clock clock_1 (.out(clock_1_out));
  // Switch switch_2: pin names not known; wires that end beside it: 1'b1, switch_2_p2, switch_2_p3
  Pull_Resistor pull_resistor_3 (.node(switch_2_p2));
  ExactlyOne xor_1 (.out(xor_1_out), .in0(or_6_out), .in1(switch_2_p2), .in2(switch_2_p2));
  Button button_6 (.out(button_6_out));
  // Digital_Oscilloscope digital_oscilloscope_1: pin names not known; wires that end beside it: clock_1_out, digital_oscilloscope_1_p2
  latch_8bit latch_8bit_1 (
    .Reset(button_7_out), .D0(alu_4bit_1_c0[0]), .D1(alu_4bit_1_c0[1]), .D2(alu_4bit_1_c0[2]),
    .D3(alu_4bit_1_c0[3]), .Enabled(or_6_out), .Q0(latch_8bit_1_q0[0]), .Q1(latch_8bit_1_q0[1]),
    .Q2(latch_8bit_1_q0[2]), .Q3(latch_8bit_1_q0[3]));  // open: D4, D5, D6, D7, Q4, Q5, Q6, Q7
  Button button_7 (.out(button_7_out));
  nor nor_1 (nor_1_out, register_1_q[0], register_1_q[1], register_1_q[2], register_1_q[3]);
  Button button_8 (.out(button_8_out));
  not not_1 (not_1_out, digital_oscilloscope_1_p2);
  and and_5 (and_5_out, digital_oscilloscope_1_p2, clock_1_out);
  and and_6 (and_6_out, clock_1_out, digital_oscilloscope_1_p2);
  Button button_9 (.out(switch_2_p3));
  Button button_10 (.out(button_10_out));
  D_Flip_Flop #(.trigger("falling")) d_ff_1 (.D(d_ff_4_q), .clk(and_7_out), .Qn(d_ff_1_qn));  // open: Q, preset, reset
  and and_7 (and_7_out, clock_1_out, not_1_out);
  D_Flip_Flop #(.trigger("falling")) d_ff_2 (.D(or_9_out), .clk(and_6_out), .Q(d_ff_2_q));  // open: Qn, preset, reset
  Register #(.width(4)) register_3 (
    .D(alu_4bit_1_zf), .clk(or_6_out), .Q(register_3_q), .clr(button_11_out));  // open: en
  Button button_11 (.out(button_11_out));
  and and_8 (and_8_out, d_ff_2_q, ~digital_oscilloscope_1_p2);  // AND_Gate
  or or_10 (or_10_out, not_1_out, digital_oscilloscope_1_p2);
  and and_9 (and_9_out, d_ff_1_qn, digital_oscilloscope_1_p2);
  D_Flip_Flop #(.trigger("falling")) d_ff_3 (.D(and_8_out), .clk(or_10_out), .Q(d_ff_3_q));  // open: Qn, preset, reset
  Pull_Resistor pull_resistor_4 (.node(pull_resistor_4_node));
  add_sub_4bit add_sub_4bit_1 (
    .A0(pull_resistor_4_node), .A1(pull_resistor_4_node), .A2(pull_resistor_4_node),
    .A3(pull_resistor_4_node), .B0(latch_8bit_1_q0[0]), .B1(latch_8bit_1_q0[1]), .B2(latch_8bit_1_q0[2]),
    .B3(latch_8bit_1_q0[3]), .AS(and_10_out), .C0(add_sub_4bit_1_c0[0]), .C1(add_sub_4bit_1_c0[1]),
    .C2(add_sub_4bit_1_c0[2]), .C3(add_sub_4bit_1_c0[3]));  // open: Cin, CF, OFlag
  D_Flip_Flop #(.trigger("falling")) d_ff_4 (.D(or_5_out), .clk(and_5_out), .Q(d_ff_4_q));  // open: Qn, preset, reset
  and and_10 (and_10_out, latch_8bit_1_q0[3], register_3_q[3]);
  Counter #(.max('hf), .width(4)) counter_1 (
    .clr(button_10_out), .clk(and_9_out), .Q(counter_1_q));  // open: load, up, count, D, carry
  Counter #(.max('h3), .width(2)) counter_2 (
    .clr(or_11_out), .clk(and_11_out), .Q(counter_2_q));  // open: load, up, count, D, carry
  or or_11 (or_11_out, button_8_out, d_ff_3_q);
  and and_11 (and_11_out, digital_oscilloscope_1_p2, ~d_ff_3_q);  // AND_Gate
  // BCD_to_7_Segment_decoder bcd_to_7_segment_decoder_1: pin names not known
  _7_Segment_Display u_7_segment_display_1 (.g(and_10_out));  // open: f, a, b, e, d, c, dp
  // _7_Segment_Display 7_segment_display_2: pin names not known; wires that end beside it: n7_segment_display_2_p1, n7_segment_display_2_p2
  T_Flip_Flop t_ff_1 (.T(1'b1), .clk(clock_1_out), .Q(digital_oscilloscope_1_p2));  // open: Qn, reset, preset
  // BCD_to_7_Segment_decoder bcd_to_7_segment_decoder_2: pin names not known
  _7_Segment_Display u_7_segment_display_3 ();  // open: g, f, a, b, e, d, c, dp
  // Binary_to_BCD_converter #(.binvalue(4)) binary_to_bcd_converter_1: pin names not known; wires that end beside it: add_sub_4bit_1_c0, n7_segment_display_2_p1, n7_segment_display_2_p2

  // Notes on the sheet:
  //   OPCODE
  //   SUB_OPCODE
  //   contents of rom_1 (hex, n*v repeats v):
  //   0 20 1
  //   SubOp Ctr Reset
  //   Op Ctr Reset
endmodule

module adder_1bit (
  input  A,
  input  B,
  input  CF_In,
  output AX_write,
  output CF_out
);

  wire and_1_out, and_2_out, xor_1_out;

  xor xor_1 (xor_1_out, A, B);
  xor xor_2 (AX_write, xor_1_out, CF_In);
  and and_1 (and_1_out, CF_In, xor_1_out);
  and and_2 (and_2_out, A, B);
  or or_1 (CF_out, and_1_out, and_2_out);

  // Notes on the sheet:
  //   1bit_adder
endmodule

module adder_4bit (
  input  A0,
  input  B0,
  input  A1,
  input  B1,
  input  A2,
  input  B2,
  input  A3,
  input  B3,
  output C0,
  output C1,
  output C2,
  output C3,
  output CF
);

  wire adder_1bit_1_cf_out, adder_1bit_2_cf_out, adder_1bit_3_cf_out;

  adder_1bit adder_1bit_1 (.A(A0), .B(B0), .AX_write(C0), .CF_out(adder_1bit_1_cf_out));  // open: CF_In
  adder_1bit adder_1bit_2 (.A(A1), .B(B1), .CF_In(adder_1bit_1_cf_out), .AX_write(C1), .CF_out(adder_1bit_2_cf_out));
  adder_1bit adder_1bit_3 (.A(A2), .B(B2), .CF_In(adder_1bit_2_cf_out), .AX_write(C2), .CF_out(adder_1bit_3_cf_out));
  adder_1bit adder_1bit_4 (.A(A3), .B(B3), .CF_In(adder_1bit_3_cf_out), .AX_write(C3), .CF_out(CF));

  // Notes on the sheet:
  //   4bit_add
endmodule

module comp_4bit (
  input  A0,
  input  A1,
  input  A2,
  input  A3,
  input  B0,
  input  B1,
  input  B2,
  input  B3,
  output X
);

  wire xor_1_out, xor_2_out, xor_3_out, xor_4_out;

  xor xor_1 (xor_1_out, A3, B3);
  xor xor_2 (xor_2_out, A2, B2);
  xor xor_3 (xor_3_out, A1, B1);
  xor xor_4 (xor_4_out, A0, B0);
  nor nor_1 (X, xor_1_out, xor_2_out, xor_3_out, xor_4_out);
endmodule

module add_sub_4bit (
  input  AS,
  input  Cin,
  input  A0,
  input  B0,
  input  A1,
  input  B1,
  input  A2,
  input  B2,
  input  A3,
  input  B3,
  output C0,
  output C1,
  output C2,
  output C3,
  output CF,
  output OFlag
);

  wire adder_1bit_1_cf_out, adder_1bit_2_cf_out, adder_1bit_3_cf_out, xor_1_out, xor_2_out, xor_3_out,
       xor_4_out, xor_5_out;

  xor xor_1 (xor_1_out, AS, B0);
  xor xor_2 (xor_2_out, AS, B1);
  xor xor_3 (xor_3_out, AS, B2);
  xor xor_4 (xor_4_out, AS, B3);
  xor xor_5 (xor_5_out, AS, Cin);
  adder_1bit adder_1bit_1 (.A(A0), .B(xor_1_out), .CF_In(xor_5_out), .AX_write(C0), .CF_out(adder_1bit_1_cf_out));
  adder_1bit adder_1bit_2 (
    .A(A1), .B(xor_2_out), .CF_In(adder_1bit_1_cf_out), .AX_write(C1), .CF_out(adder_1bit_2_cf_out));
  adder_1bit adder_1bit_3 (
    .A(A2), .B(xor_3_out), .CF_In(adder_1bit_2_cf_out), .AX_write(C2), .CF_out(adder_1bit_3_cf_out));
  adder_1bit adder_1bit_4 (.A(A3), .B(xor_4_out), .CF_In(adder_1bit_3_cf_out), .AX_write(C3), .CF_out(CF));
  xor xor_6 (OFlag, adder_1bit_3_cf_out, CF);

  // Notes on the sheet:
  //   4bit_add/sub
endmodule

module ALU_4bit (
  input  [3:0] in_1,
  input  Enable,
  input  Latch,
  input  A0,
  input  Cin,
  input  A1,
  input  A2,
  input  A3,
  input  B0,
  input  B1,
  input  B3,
  input  B4,
  input  Sign,
  input  Reset,
  output C0,
  output C1,
  output C2,
  output C3,
  output ZF,
  output CF,
  output OFlag,
  output SF
);

  wire add_sub_4bit_1_c0, add_sub_4bit_1_c1, add_sub_4bit_1_c2, add_sub_4bit_1_c3, add_sub_4bit_1_cf,
       add_sub_4bit_1_oflag, decoder_1_out2, decoder_1_out3, decoder_1_out7, latch_8bit_1_q0,
       latch_8bit_1_q1, latch_8bit_1_q2, latch_8bit_1_q3, latch_8bit_1_q4, latch_8bit_1_q5, latch_8bit_1_q6,
       latch_8bit_1_q7, n74125_1_pin9, n74125_1_pin12, nor_1_out, not_1_out, not_2_out, not_3_out, not_4_out;

  latch_8bit latch_8bit_1 (
    .Reset(Reset), .D0(A0), .D1(A1), .D2(A2), .D3(A3), .D4(B0), .D5(B1), .D6(B3), .D7(B4), .Enabled(Latch),
    .Q0(latch_8bit_1_q0), .Q1(latch_8bit_1_q1), .Q2(latch_8bit_1_q2), .Q3(latch_8bit_1_q3),
    .Q4(latch_8bit_1_q4), .Q5(latch_8bit_1_q5), .Q6(latch_8bit_1_q6), .Q7(latch_8bit_1_q7));
  Decoder #(.select(4)) decoder_1 (
    .out2(decoder_1_out2), .out3(decoder_1_out3), .out7(decoder_1_out7), .sel(in_1), .en(Enable));  // open: out0, out1, out4, out5, out6, out8, out9, out10, out11, out12, out13, out14, out15
  not not_1 (not_1_out, decoder_1_out7);
  add_sub_4bit add_sub_4bit_1 (
    .A0(latch_8bit_1_q0), .A1(latch_8bit_1_q1), .A2(latch_8bit_1_q2), .A3(latch_8bit_1_q3),
    .B0(latch_8bit_1_q4), .B1(latch_8bit_1_q5), .B2(latch_8bit_1_q6), .B3(latch_8bit_1_q7),
    .AS(decoder_1_out3), .Cin(Cin), .C0(add_sub_4bit_1_c0), .C1(add_sub_4bit_1_c1), .C2(add_sub_4bit_1_c2),
    .C3(add_sub_4bit_1_c3), .CF(add_sub_4bit_1_cf), .OFlag(add_sub_4bit_1_oflag));
  not not_2 (not_2_out, latch_8bit_1_q0);
  not not_3 (not_3_out, latch_8bit_1_q1);
  nor nor_1 (nor_1_out, decoder_1_out2, decoder_1_out3);
  _74125 #(.ShowInternalStructure("true")) u_74125_1 (
    .pin1(not_1_out), .pin2(not_2_out), .pin3(C0), .pin4(not_1_out), .pin5(not_3_out), .pin6(C1),
    .pin13(not_1_out), .pin12(n74125_1_pin12), .pin11(C2), .pin10(not_1_out), .pin9(n74125_1_pin9), .pin8(C3));
  not not_4 (not_4_out, Sign);
  not not_5 (n74125_1_pin9, latch_8bit_1_q3);
  _74125 #(.ShowInternalStructure("true")) u_74125_2 (
    .pin1(nor_1_out), .pin2(add_sub_4bit_1_c0), .pin3(C0), .pin4(nor_1_out), .pin5(add_sub_4bit_1_c1),
    .pin6(C1), .pin13(nor_1_out), .pin12(add_sub_4bit_1_c2), .pin11(C2), .pin10(nor_1_out),
    .pin9(add_sub_4bit_1_c3), .pin8(C3));
  and and_1 (CF, add_sub_4bit_1_cf, not_4_out);
  and and_2 (OFlag, Sign, add_sub_4bit_1_oflag);
  and and_3 (SF, add_sub_4bit_1_c3, Sign);
  not not_6 (n74125_1_pin12, latch_8bit_1_q2);
  nor nor_2 (ZF, add_sub_4bit_1_c0, add_sub_4bit_1_c1, add_sub_4bit_1_c2, add_sub_4bit_1_c3);

  // Notes on the sheet:
  //   add
  //   sub
  //   not
endmodule

module latch_8bit (
  input  Enabled,
  input  D0,
  input  D1,
  input  D2,
  input  D3,
  input  D4,
  input  D5,
  input  D6,
  input  D7,
  input  Reset,
  output Q0,
  output Q1,
  output Q2,
  output Q3,
  output Q4,
  output Q5,
  output Q6,
  output Q7
);

  D_Flip_Flop #(.trigger("high")) d_ff_1 (.D(D0), .clk(Enabled), .Q(Q0), .reset(Reset));  // open: Qn, preset
  D_Flip_Flop #(.trigger("high")) d_ff_2 (.D(D1), .clk(Enabled), .Q(Q1), .reset(Reset));  // open: Qn, preset
  D_Flip_Flop #(.trigger("high")) d_ff_3 (.D(D2), .clk(Enabled), .Q(Q2), .reset(Reset));  // open: Qn, preset
  D_Flip_Flop #(.trigger("high")) d_ff_4 (.D(D3), .clk(Enabled), .Q(Q3), .reset(Reset));  // open: Qn, preset
  D_Flip_Flop #(.trigger("high")) d_ff_5 (.D(D4), .clk(Enabled), .Q(Q4), .reset(Reset));  // open: Qn, preset
  D_Flip_Flop #(.trigger("high")) d_ff_6 (.D(D5), .clk(Enabled), .Q(Q5), .reset(Reset));  // open: Qn, preset
  D_Flip_Flop #(.trigger("high")) d_ff_7 (.D(D6), .clk(Enabled), .Q(Q6), .reset(Reset));  // open: Qn, preset
  D_Flip_Flop #(.trigger("high")) d_ff_8 (.D(D7), .clk(Enabled), .Q(Q7), .reset(Reset));  // open: Qn, preset

  // Notes on the sheet:
  //   8bit latch
endmodule

module test (
);

  wire add_sub_4bit_1_c0, add_sub_4bit_1_c1, add_sub_4bit_1_c2, add_sub_4bit_1_c3, add_sub_4bit_1_cf,
       add_sub_4bit_1_oflag, alu_4bit_1_c0, alu_4bit_1_c1, alu_4bit_1_c2, alu_4bit_1_c3, alu_4bit_1_cf,
       alu_4bit_1_oflag, alu_4bit_1_sf, alu_4bit_1_zf, and_1_out, and_2_out, and_3_out, dipswitch_1_p1,
       dipswitch_1_p2, dipswitch_2_p1, dipswitch_2_p2, dipswitch_2_p3, dipswitch_2_p4, dipswitch_2_p5,
       dipswitch_2_p6, dipswitch_4_p1, dipswitch_4_p2, dipswitch_4_p3, dipswitch_4_p4, dipswitch_5_p1,
       dipswitch_5_p2, dipswitch_5_p3, dipswitch_5_p4, dipswitch_6_p1, dipswitch_6_p2, dipswitch_6_p3,
       dipswitch_6_p4, n7_segment_display_2_p1, n7_segment_display_2_p2, nor_1_out, not_1_out,
       pull_resistor_1_node, pull_resistor_4_node, switch_2_p2, switch_3_p2;
  wire [3:0] add_sub_4bit_2_c0, dipswitch_3_p4, rom_1_data;

  Pull_Resistor pull_resistor_1 (.node(pull_resistor_1_node));
  // Switch switch_1: pin names not known; wires that end beside it: 1'b1, pull_resistor_1_node
  // DipSwitch #(.number(4)) dipswitch_1: pin names not known; wires that end beside it: dipswitch_1_p1, dipswitch_1_p2
  add_sub_4bit add_sub_4bit_1 (
    .A0(dipswitch_1_p1), .A1(dipswitch_1_p2), .A2(dipswitch_2_p1), .A3(dipswitch_2_p2), .B0(dipswitch_2_p3),
    .B1(dipswitch_2_p4), .B2(dipswitch_2_p5), .B3(dipswitch_2_p6), .AS(pull_resistor_1_node),
    .Cin(switch_3_p2), .C0(add_sub_4bit_1_c0), .C1(add_sub_4bit_1_c1), .C2(add_sub_4bit_1_c2),
    .C3(add_sub_4bit_1_c3), .CF(add_sub_4bit_1_cf), .OFlag(add_sub_4bit_1_oflag));
  // DipSwitch #(.number(4)) dipswitch_2: pin names not known; wires that end beside it: dipswitch_2_p1, dipswitch_2_p2, dipswitch_2_p3, dipswitch_2_p4, dipswitch_2_p5, dipswitch_2_p6
  // Switch switch_2: pin names not known; wires that end beside it: 1'b1, switch_2_p2
  Pull_Resistor pull_resistor_2 (.node(switch_2_p2));
  // Switch switch_3: pin names not known; wires that end beside it: 1'b1, switch_3_p2
  Pull_Resistor pull_resistor_3 (.node(switch_3_p2));
  LED led_1 (.in(add_sub_4bit_1_c0));
  LED led_2 (.in(add_sub_4bit_1_c1));
  LED led_3 (.in(add_sub_4bit_1_c2));
  LED led_4 (.in(add_sub_4bit_1_c3));
  nor nor_1 (nor_1_out, add_sub_4bit_1_c3, add_sub_4bit_1_c2, add_sub_4bit_1_c1, add_sub_4bit_1_c0);
  and and_1 (and_1_out, add_sub_4bit_1_cf, not_1_out);
  LED led_5 (.in(and_1_out));
  not not_1 (not_1_out, switch_2_p2);
  and and_2 (and_2_out, switch_2_p2, add_sub_4bit_1_oflag);
  LED led_6 (.in(and_2_out));
  LED led_7 (.in(switch_2_p2));
  Pull_Resistor pull_resistor_4 (.node(pull_resistor_4_node));
  add_sub_4bit add_sub_4bit_2 (
    .A0(pull_resistor_4_node), .A1(pull_resistor_4_node), .A2(pull_resistor_4_node),
    .A3(pull_resistor_4_node), .B0(add_sub_4bit_1_c0), .B1(add_sub_4bit_1_c1), .B2(add_sub_4bit_1_c2),
    .B3(add_sub_4bit_1_c3), .AS(and_3_out), .C0(add_sub_4bit_2_c0[0]), .C1(add_sub_4bit_2_c0[1]),
    .C2(add_sub_4bit_2_c0[2]), .C3(add_sub_4bit_2_c0[3]));  // open: Cin, CF, OFlag
  LED led_8 (.in(nor_1_out));
  and and_3 (and_3_out, add_sub_4bit_1_c3, switch_2_p2);
  // BCD_to_7_Segment_decoder bcd_to_7_segment_decoder_1: pin names not known
  _7_Segment_Display u_7_segment_display_1 (.g(and_3_out));  // open: f, a, b, e, d, c, dp
  // _7_Segment_Display 7_segment_display_2: pin names not known; wires that end beside it: n7_segment_display_2_p1, n7_segment_display_2_p2
  // BCD_to_7_Segment_decoder bcd_to_7_segment_decoder_2: pin names not known
  _7_Segment_Display u_7_segment_display_3 ();  // open: g, f, a, b, e, d, c, dp
  // Binary_to_BCD_converter #(.binvalue(4)) binary_to_bcd_converter_1: pin names not known; wires that end beside it: add_sub_4bit_2_c0, n7_segment_display_2_p1, n7_segment_display_2_p2
  // DipSwitch #(.number(4)) dipswitch_3: pin names not known; wires that end beside it: dipswitch_3_p4[3], dipswitch_3_p4[2], dipswitch_3_p4[1], dipswitch_3_p4[0]
  ROM #(.addrWidth(4), .dataWidth(4)) rom_1 (.addr(dipswitch_3_p4), .data(rom_1_data));
  ALU_4bit alu_4bit_1 (
    .Enable(dipswitch_4_p3), .Latch(dipswitch_4_p4), .A0(dipswitch_5_p1), .A1(dipswitch_5_p2),
    .A2(dipswitch_5_p3), .A3(dipswitch_5_p4), .B0(dipswitch_6_p1), .B1(dipswitch_6_p2), .B3(dipswitch_6_p3),
    .B4(dipswitch_6_p4), .Sign(dipswitch_4_p2), .in_1(rom_1_data), .Cin(dipswitch_4_p1), .C0(alu_4bit_1_c0),
    .C1(alu_4bit_1_c1), .C2(alu_4bit_1_c2), .C3(alu_4bit_1_c3), .ZF(alu_4bit_1_zf), .CF(alu_4bit_1_cf),
    .OFlag(alu_4bit_1_oflag), .SF(alu_4bit_1_sf));  // open: Reset
  // DipSwitch #(.number(4)) dipswitch_4: pin names not known; wires that end beside it: dipswitch_4_p1, dipswitch_4_p2, dipswitch_4_p3, dipswitch_4_p4
  // DipSwitch #(.number(4)) dipswitch_5: pin names not known; wires that end beside it: dipswitch_5_p1, dipswitch_5_p2, dipswitch_5_p3, dipswitch_5_p4
  LedBar #(.matrixcols(4)) ledbar_1 (
    .led0(alu_4bit_1_c0), .led1(alu_4bit_1_c1), .led2(alu_4bit_1_c2), .led3(alu_4bit_1_c3));
  // DipSwitch #(.number(4)) dipswitch_6: pin names not known; wires that end beside it: dipswitch_6_p1, dipswitch_6_p2, dipswitch_6_p3, dipswitch_6_p4
  LedBar #(.matrixcols(4)) ledbar_2 (
    .led0(alu_4bit_1_zf), .led1(alu_4bit_1_cf), .led2(alu_4bit_1_oflag), .led3(alu_4bit_1_sf));

  // Notes on the sheet:
  //   Add or Sub
  //   Unsigned or Signed
  //   Carry IN
  //   SF
  //   CF
  //   OF
  //   SF
  //   ZF
  //   contents of rom_1 (hex, n*v repeats v):
  //   2
endmodule

module add_sub_8bit (
  input  AS,
  input  Cin,
  input  Enable,
  input  A0,
  input  B0,
  input  A1,
  input  B1,
  input  A2,
  input  B2,
  input  A3,
  input  B3,
  input  A4,
  input  B4,
  input  A5,
  input  B5,
  input  A6,
  input  B6,
  input  A7,
  input  B7,
  output C0,
  output C1,
  output C2,
  output C3,
  output C4,
  output C5,
  output C6,
  output C7,
  output CF,
  output OFlag
);

  wire adder_1bit_1_ax_write, adder_1bit_1_cf_out, adder_1bit_2_ax_write, adder_1bit_2_cf_out,
       adder_1bit_3_ax_write, adder_1bit_3_cf_out, adder_1bit_4_ax_write, adder_1bit_4_cf_out,
       adder_1bit_5_ax_write, adder_1bit_5_cf_out, adder_1bit_6_ax_write, adder_1bit_6_cf_out,
       adder_1bit_7_ax_write, adder_1bit_7_cf_out, adder_1bit_8_ax_write, adder_1bit_8_cf_out, xor_1_out,
       xor_2_out, xor_3_out, xor_4_out, xor_5_out, xor_6_out, xor_7_out, xor_8_out, xor_9_out;

  xor xor_1 (xor_1_out, AS, B0);
  xor xor_2 (xor_2_out, AS, B1);
  xor xor_3 (xor_3_out, AS, B2);
  xor xor_4 (xor_4_out, AS, B3);
  xor xor_5 (xor_5_out, AS, B4);
  xor xor_6 (xor_6_out, AS, B5);
  xor xor_7 (xor_7_out, AS, B6);
  xor xor_8 (xor_8_out, AS, B7);
  xor xor_9 (xor_9_out, AS, Cin);
  adder_1bit adder_1bit_1 (
    .A(A0), .B(xor_1_out), .CF_In(xor_9_out), .AX_write(adder_1bit_1_ax_write), .CF_out(adder_1bit_1_cf_out));
  adder_1bit adder_1bit_2 (
    .A(A1), .B(xor_2_out), .CF_In(adder_1bit_1_cf_out), .AX_write(adder_1bit_2_ax_write),
    .CF_out(adder_1bit_2_cf_out));
  adder_1bit adder_1bit_3 (
    .A(A2), .B(xor_3_out), .CF_In(adder_1bit_2_cf_out), .AX_write(adder_1bit_3_ax_write),
    .CF_out(adder_1bit_3_cf_out));
  adder_1bit adder_1bit_4 (
    .A(A3), .B(xor_4_out), .CF_In(adder_1bit_3_cf_out), .AX_write(adder_1bit_4_ax_write),
    .CF_out(adder_1bit_4_cf_out));
  adder_1bit adder_1bit_5 (
    .A(A4), .B(xor_5_out), .CF_In(adder_1bit_4_cf_out), .AX_write(adder_1bit_5_ax_write),
    .CF_out(adder_1bit_5_cf_out));
  adder_1bit adder_1bit_6 (
    .A(A5), .B(xor_6_out), .CF_In(adder_1bit_5_cf_out), .AX_write(adder_1bit_6_ax_write),
    .CF_out(adder_1bit_6_cf_out));
  adder_1bit adder_1bit_7 (
    .A(A6), .B(xor_7_out), .CF_In(adder_1bit_6_cf_out), .AX_write(adder_1bit_7_ax_write),
    .CF_out(adder_1bit_7_cf_out));
  adder_1bit adder_1bit_8 (
    .A(A7), .B(xor_8_out), .CF_In(adder_1bit_7_cf_out), .AX_write(adder_1bit_8_ax_write),
    .CF_out(adder_1bit_8_cf_out));
  assign C0 = Enable ? adder_1bit_1_ax_write : 1'bz;  // Controlled_Buffer controlled_buffer_1
  assign C1 = Enable ? adder_1bit_2_ax_write : 1'bz;  // Controlled_Buffer controlled_buffer_2
  assign C2 = Enable ? adder_1bit_3_ax_write : 1'bz;  // Controlled_Buffer controlled_buffer_3
  assign C3 = Enable ? adder_1bit_4_ax_write : 1'bz;  // Controlled_Buffer controlled_buffer_4
  assign C4 = Enable ? adder_1bit_5_ax_write : 1'bz;  // Controlled_Buffer controlled_buffer_5
  assign C5 = Enable ? adder_1bit_6_ax_write : 1'bz;  // Controlled_Buffer controlled_buffer_6
  assign C6 = Enable ? adder_1bit_7_ax_write : 1'bz;  // Controlled_Buffer controlled_buffer_7
  assign C7 = Enable ? adder_1bit_8_ax_write : 1'bz;  // Controlled_Buffer controlled_buffer_8
  xor xor_10 (CF, adder_1bit_8_cf_out, AS);
  xor xor_11 (OFlag, adder_1bit_7_cf_out, adder_1bit_8_cf_out);

  // Notes on the sheet:
  //   8bit_add/sub
endmodule

module ALU_8bit (
  input  Cin,
  input  Enable,
  input  Latch,
  input  [3:0] OPcode,
  input  A0,
  input  A1,
  input  A2,
  input  A3,
  input  A4,
  input  A5,
  input  A6,
  input  A7,
  input  B0,
  input  B1,
  input  B2,
  input  B3,
  input  B4,
  input  B5,
  input  B6,
  input  B7,
  input  Reset,
  output C0,
  output C1,
  output C2,
  output ZF,
  output C3,
  output C4,
  output C5,
  output CF,
  output C6,
  output C7,
  output OFlag,
  output SF
);

  wire add_sub_8bit_1_cf, add_sub_8bit_1_oflag, bcd_to_7_segment_decoder_4_p1, bcd_to_7_segment_decoder_8_p1,
       binary_to_bcd_converter_1_p2, binary_to_bcd_converter_1_p4, binary_to_bcd_converter_2_p2,
       binary_to_bcd_converter_2_p4, binary_to_bcd_converter_2_p5, binary_to_bcd_converter_3_p2,
       binary_to_bcd_converter_3_p5, button_1_out, button_2_out, button_3_out, controlled_buffer_6_out,
       controlled_buffer_8_out, controlled_buffer_9_out, controlled_buffer_24_out, decoder_1_out0,
       decoder_1_out1, decoder_1_out2, decoder_1_out3, decoder_1_out4, decoder_1_out5, decoder_1_out6,
       decoder_1_out7, decoder_1_out8, decoder_1_out9, decoder_1_out10, decoder_1_out11, decoder_1_out12,
       decoder_1_out13, decoder_1_out14, nor_1_out, nor_2_out, not_1_out, not_2_out, not_3_out, not_4_out,
       not_5_out, or_1_out, or_2_out, or_3_out, or_4_out, or_7_out, or_9_out, or_12_out, or_15_out,
       or_17_out, or_18_out, or_19_out, xor_9_out;
  wire [7:0] and_8_out, controlled_buffer_1_out, controlled_buffer_2_out, controlled_buffer_5_out,
       latch_8bit_1_q0, latch_8bit_2_q0, not_13_out, or_16_out, register_1_q, register_2_q, xor_8_out;

  latch_8bit latch_8bit_1 (
    .Reset(or_1_out), .D0(A0), .D1(A1), .D2(A2), .D3(A3), .D4(A4), .D5(A5), .D6(A6), .D7(A7),
    .Enabled(Latch), .Q0(latch_8bit_1_q0[0]), .Q1(latch_8bit_1_q0[1]), .Q2(latch_8bit_1_q0[2]),
    .Q3(latch_8bit_1_q0[3]), .Q4(latch_8bit_1_q0[4]), .Q5(latch_8bit_1_q0[5]), .Q6(latch_8bit_1_q0[6]),
    .Q7(latch_8bit_1_q0[7]));
  latch_8bit latch_8bit_2 (
    .Reset(or_1_out), .D0(B0), .D1(B1), .D2(B2), .D3(B3), .D4(B4), .D5(B5), .D6(B6), .D7(B7),
    .Enabled(Latch), .Q0(latch_8bit_2_q0[0]), .Q1(latch_8bit_2_q0[1]), .Q2(latch_8bit_2_q0[2]),
    .Q3(latch_8bit_2_q0[3]), .Q4(latch_8bit_2_q0[4]), .Q5(latch_8bit_2_q0[5]), .Q6(latch_8bit_2_q0[6]),
    .Q7(latch_8bit_2_q0[7]));
  Button button_1 (.out(button_1_out));
  Decoder #(.select(4)) decoder_1 (
    .out0(decoder_1_out0), .out1(decoder_1_out1), .out2(decoder_1_out2), .out3(decoder_1_out3),
    .out4(decoder_1_out4), .out5(decoder_1_out5), .out6(decoder_1_out6), .out7(decoder_1_out7),
    .out8(decoder_1_out8), .out9(decoder_1_out9), .out10(decoder_1_out10), .out11(decoder_1_out11),
    .out12(decoder_1_out12), .out13(decoder_1_out13), .out14(decoder_1_out14), .sel(OPcode), .en(Enable));  // open: out15
  or or_1 (or_1_out, Reset, button_1_out);
  or or_2 (or_2_out, decoder_1_out14, decoder_1_out13, decoder_1_out11, decoder_1_out6, decoder_1_out5, decoder_1_out4);
  and and_1 (and_8_out[7], controlled_buffer_2_out[7], controlled_buffer_1_out[7]);
  assign controlled_buffer_1_out = Latch ? latch_8bit_1_q0 : 8'bz;  // Controlled_Buffer controlled_buffer_1
  assign controlled_buffer_2_out = Latch ? latch_8bit_2_q0 : 8'bz;  // Controlled_Buffer controlled_buffer_2
  and and_2 (and_8_out[6], controlled_buffer_2_out[6], controlled_buffer_1_out[6]);
  and and_3 (and_8_out[5], controlled_buffer_2_out[5], controlled_buffer_1_out[5]);
  and and_4 (and_8_out[4], controlled_buffer_2_out[4], controlled_buffer_1_out[4]);
  or or_3 (or_3_out, decoder_1_out9, decoder_1_out3, Cin, decoder_1_out1, decoder_1_out10);
  Register register_1 (.Q(register_1_q), .clr(button_2_out));  // open: D, en, clk
  Button button_2 (.out(button_2_out));
  assign controlled_buffer_1_out = not_1_out ? register_1_q : 8'bz;  // Controlled_Buffer controlled_buffer_3
  not not_1 (not_1_out, Latch);
  Register register_2 (.Q(register_2_q), .clr(button_3_out));  // open: D, en, clk
  Button button_3 (.out(button_3_out));
  assign controlled_buffer_2_out = not_1_out ? register_2_q : 8'bz;  // Controlled_Buffer controlled_buffer_4
  and and_5 (and_8_out[3], controlled_buffer_2_out[3], controlled_buffer_1_out[3]);
  assign controlled_buffer_5_out = decoder_1_out4 ? and_8_out : 8'bz;  // Controlled_Buffer controlled_buffer_5
  or or_4 (or_4_out, decoder_1_out6, decoder_1_out5, decoder_1_out4);
  // BCD_to_7_Segment_decoder bcd_to_7_segment_decoder_1: pin names not known
  _7_Segment_Display u_7_segment_display_1 ();  // open: g, f, a, b, e, d, c, dp
  // Binary_to_BCD_converter #(.binvalue(8)) binary_to_bcd_converter_1: pin names not known; wires that end beside it: controlled_buffer_1_out, binary_to_bcd_converter_1_p2, binary_to_bcd_converter_1_p2, binary_to_bcd_converter_1_p4
  // BCD_to_7_Segment_decoder bcd_to_7_segment_decoder_2: pin names not known
  _7_Segment_Display u_7_segment_display_2 ();  // open: g, f, a, b, e, d, c, dp
  // Binary_to_BCD_converter #(.binvalue(8)) binary_to_bcd_converter_2: pin names not known; wires that end beside it: controlled_buffer_2_out, binary_to_bcd_converter_2_p2, binary_to_bcd_converter_2_p2, binary_to_bcd_converter_2_p4, binary_to_bcd_converter_2_p5
  and and_6 (and_8_out[2], controlled_buffer_2_out[2], controlled_buffer_1_out[2]);
  and and_7 (and_8_out[1], controlled_buffer_2_out[1], controlled_buffer_1_out[1]);
  // BCD_to_7_Segment_decoder bcd_to_7_segment_decoder_3: pin names not known; wires that end beside it: binary_to_bcd_converter_1_p4
  // BCD_to_7_Segment_decoder bcd_to_7_segment_decoder_4: pin names not known; wires that end beside it: bcd_to_7_segment_decoder_4_p1
  _7_Segment_Display u_7_segment_display_3 ();  // open: g, f, a, b, e, d, c, dp
  _7_Segment_Display u_7_segment_display_4 ();  // open: g, f, a, b, e, d, c, dp
  // BCD_to_7_Segment_decoder bcd_to_7_segment_decoder_5: pin names not known; wires that end beside it: binary_to_bcd_converter_2_p4
  // BCD_to_7_Segment_decoder bcd_to_7_segment_decoder_6: pin names not known; wires that end beside it: bcd_to_7_segment_decoder_4_p1, binary_to_bcd_converter_2_p5
  _7_Segment_Display u_7_segment_display_5 ();  // open: g, f, a, b, e, d, c, dp
  _7_Segment_Display u_7_segment_display_6 ();  // open: g, f, a, b, e, d, c, dp
  and and_8 (and_8_out[0], controlled_buffer_2_out[0], controlled_buffer_1_out[0]);
  or or_5 (or_16_out[7], controlled_buffer_2_out[7], controlled_buffer_1_out[7]);
  or or_6 (or_16_out[6], controlled_buffer_2_out[6], controlled_buffer_1_out[6]);
  assign controlled_buffer_6_out = or_2_out ? controlled_buffer_5_out[7] : 1'bz;  // Controlled_Buffer controlled_buffer_6
  or or_7 (or_7_out, decoder_1_out10, decoder_1_out8, decoder_1_out3, decoder_1_out2);
  or or_8 (or_16_out[5], controlled_buffer_2_out[5], controlled_buffer_1_out[5]);
  or or_9 (or_9_out, decoder_1_out3, decoder_1_out8, decoder_1_out10, decoder_1_out2, decoder_1_out9, decoder_1_out0, decoder_1_out1);
  add_sub_8bit add_sub_8bit_1 (
    .A0(controlled_buffer_1_out[0]), .A1(controlled_buffer_1_out[1]), .A2(controlled_buffer_1_out[2]),
    .A3(controlled_buffer_1_out[3]), .A4(controlled_buffer_1_out[4]), .A5(controlled_buffer_1_out[5]),
    .A6(controlled_buffer_1_out[6]), .A7(controlled_buffer_1_out[7]), .B0(controlled_buffer_2_out[0]),
    .B1(controlled_buffer_2_out[1]), .B2(controlled_buffer_2_out[2]), .B3(controlled_buffer_2_out[3]),
    .B4(controlled_buffer_2_out[4]), .B5(controlled_buffer_2_out[5]), .B6(controlled_buffer_2_out[6]),
    .B7(controlled_buffer_2_out[7]), .AS(or_7_out), .Cin(or_3_out), .Enable(or_9_out),
    .OFlag(add_sub_8bit_1_oflag), .C0(controlled_buffer_5_out[0]), .C1(controlled_buffer_5_out[1]),
    .C2(controlled_buffer_5_out[2]), .C3(controlled_buffer_5_out[3]), .C4(controlled_buffer_5_out[4]),
    .C5(controlled_buffer_5_out[5]), .C6(controlled_buffer_5_out[6]), .C7(controlled_buffer_5_out[7]),
    .CF(add_sub_8bit_1_cf));
  or or_10 (or_16_out[3], controlled_buffer_2_out[3], controlled_buffer_1_out[3]);
  or or_11 (or_16_out[4], controlled_buffer_2_out[4], controlled_buffer_1_out[4]);
  or or_12 (or_12_out, decoder_1_out8, decoder_1_out9, decoder_1_out0, decoder_1_out1);
  or or_13 (or_16_out[2], controlled_buffer_2_out[2], controlled_buffer_1_out[2]);
  assign controlled_buffer_5_out = decoder_1_out5 ? or_16_out : 8'bz;  // Controlled_Buffer controlled_buffer_7
  or or_14 (or_16_out[1], controlled_buffer_2_out[1], controlled_buffer_1_out[1]);
  not not_2 (not_2_out, Enable);
  or or_15 (or_15_out, decoder_1_out7, not_2_out);
  or or_16 (or_16_out[0], controlled_buffer_2_out[0], controlled_buffer_1_out[0]);
  assign controlled_buffer_8_out = or_12_out ? add_sub_8bit_1_cf : 1'bz;  // Controlled_Buffer controlled_buffer_8
  assign controlled_buffer_9_out = or_9_out ? add_sub_8bit_1_oflag : 1'bz;  // Controlled_Buffer controlled_buffer_9
  assign controlled_buffer_6_out = or_9_out ? controlled_buffer_5_out[7] : 1'bz;  // Controlled_Buffer controlled_buffer_10
  not not_3 (not_3_out, Enable);
  assign controlled_buffer_8_out = or_4_out ? 1'b0 : 1'bz;  // Controlled_Buffer controlled_buffer_11
  assign controlled_buffer_9_out = or_4_out ? 1'b0 : 1'bz;  // Controlled_Buffer controlled_buffer_12
  assign controlled_buffer_6_out = decoder_1_out12 ? 1'b0 : 1'bz;  // Controlled_Buffer controlled_buffer_13
  xor xor_1 (xor_8_out[7], controlled_buffer_2_out[7], controlled_buffer_1_out[7]);
  xor xor_2 (xor_8_out[6], controlled_buffer_2_out[6], controlled_buffer_1_out[6]);
  or or_17 (or_17_out, not_3_out, decoder_1_out8);
  xor xor_3 (xor_8_out[5], controlled_buffer_2_out[5], controlled_buffer_1_out[5]);
  assign {C7, C6, C5, C4, C3, C2, C1, C0} = not_4_out ? controlled_buffer_5_out : 8'bz;  // Controlled_Buffer controlled_buffer_14
  not not_4 (not_4_out, or_17_out);
  nor nor_1 (nor_1_out, controlled_buffer_5_out[0], controlled_buffer_5_out[1], controlled_buffer_5_out[2], controlled_buffer_5_out[3], controlled_buffer_5_out[4], controlled_buffer_5_out[5], controlled_buffer_5_out[6], controlled_buffer_5_out[7]);
  assign ZF = not_5_out ? nor_1_out : 1'bz;  // Controlled_Buffer controlled_buffer_15
  not not_5 (not_5_out, or_15_out);
  xor xor_4 (xor_8_out[4], controlled_buffer_2_out[4], controlled_buffer_1_out[4]);
  // BCD_to_7_Segment_decoder bcd_to_7_segment_decoder_7: pin names not known
  // BCD_to_7_Segment_decoder bcd_to_7_segment_decoder_8: pin names not known; wires that end beside it: bcd_to_7_segment_decoder_8_p1
  _7_Segment_Display u_7_segment_display_7 ();  // open: g, f, a, b, e, d, c, dp
  _7_Segment_Display u_7_segment_display_8 ();  // open: g, f, a, b, e, d, c, dp
  // Binary_to_BCD_converter #(.binvalue(8)) binary_to_bcd_converter_3: pin names not known; wires that end beside it: controlled_buffer_5_out, binary_to_bcd_converter_3_p2, binary_to_bcd_converter_3_p2, bcd_to_7_segment_decoder_8_p1, binary_to_bcd_converter_3_p5
  assign CF = Enable ? controlled_buffer_8_out : 1'bz;  // Controlled_Buffer controlled_buffer_16
  assign OFlag = Enable ? controlled_buffer_9_out : 1'bz;  // Controlled_Buffer controlled_buffer_17
  assign SF = Enable ? controlled_buffer_6_out : 1'bz;  // Controlled_Buffer controlled_buffer_18
  xor xor_5 (xor_8_out[3], controlled_buffer_2_out[3], controlled_buffer_1_out[3]);
  xor xor_6 (xor_8_out[2], controlled_buffer_2_out[2], controlled_buffer_1_out[2]);
  assign controlled_buffer_5_out = decoder_1_out6 ? xor_8_out : 8'bz;  // Controlled_Buffer controlled_buffer_19
  // BCD_to_7_Segment_decoder bcd_to_7_segment_decoder_9: pin names not known; wires that end beside it: binary_to_bcd_converter_3_p5
  _7_Segment_Display u_7_segment_display_9 ();  // open: g, f, a, b, e, d, c, dp
  xor xor_7 (xor_8_out[1], controlled_buffer_2_out[1], controlled_buffer_1_out[1]);
  xor xor_8 (xor_8_out[0], controlled_buffer_2_out[0], controlled_buffer_1_out[0]);
  or or_18 (or_18_out, decoder_1_out14, decoder_1_out12);
  or or_19 (or_19_out, decoder_1_out13, decoder_1_out11);
  not not_6 (not_13_out[7], controlled_buffer_1_out[7]);
  not not_7 (not_13_out[6], controlled_buffer_1_out[6]);
  not not_8 (not_13_out[5], controlled_buffer_1_out[5]);
  assign controlled_buffer_5_out = decoder_1_out7 ? not_13_out : 8'bz;  // Controlled_Buffer controlled_buffer_20
  not not_9 (not_13_out[4], controlled_buffer_1_out[4]);
  not not_10 (not_13_out[3], controlled_buffer_1_out[3]);
  not not_11 (not_13_out[2], controlled_buffer_1_out[2]);
  not not_12 (not_13_out[1], controlled_buffer_1_out[1]);
  nor nor_2 (nor_2_out, decoder_1_out13, decoder_1_out14);
  not not_13 (not_13_out[0], controlled_buffer_1_out[0]);
  assign controlled_buffer_5_out = or_19_out ? {controlled_buffer_1_out[6:0], Cin} : 8'bz;  // Controlled_Buffer controlled_buffer_21
  assign controlled_buffer_9_out = nor_2_out ? controlled_buffer_24_out : 1'bz;  // Controlled_Buffer controlled_buffer_22
  assign controlled_buffer_8_out = or_19_out ? controlled_buffer_1_out[7] : 1'bz;  // Controlled_Buffer controlled_buffer_23
  xor xor_9 (xor_9_out, controlled_buffer_1_out[7], controlled_buffer_1_out[6]);
  assign controlled_buffer_24_out = or_19_out ? xor_9_out : 1'bz;  // Controlled_Buffer controlled_buffer_24
  assign controlled_buffer_24_out = or_18_out ? controlled_buffer_1_out[7] : 1'bz;  // Controlled_Buffer controlled_buffer_25
  assign controlled_buffer_8_out = or_18_out ? controlled_buffer_1_out[0] : 1'bz;  // Controlled_Buffer controlled_buffer_26
  assign controlled_buffer_5_out = or_18_out ? {Cin, controlled_buffer_1_out[7:1]} : 8'bz;  // Controlled_Buffer controlled_buffer_27

  // Notes on the sheet:
  //   add
  //   adc
  //   and
  //   or
  //   xor
  //   cmp
  //   dec
  //   shl
  //   shr
  //   rol
  //   ror
  //   sub
  //   sbb
  //   not
  //   inc
  //   AND
  //   IN A
  //   IN B
  //   SF
  //   OR
  //   XOR
  //   OUTPUT
  //   ror
  //   rol
  //   shr
  //   shl
  //   SHR/ROR
  //   SHL/ROL
  //   Coupling
  //   ROR/ROL OF decider
  //   NOT
  //   of
  //   cin
  //   cf
  //   SHL
  //   ROL
  //   SHR
  //   ROR
endmodule

module main_8bit (
);

  wire decoder_1_out1, decoder_1_out2, decoder_2_out2;
  wire [7:0] register_1_q;

  Register register_1 (.Q(register_1_q));  // open: D, en, clk, clr
  Decoder #(.select(4)) decoder_1 (
    .out1(decoder_1_out1), .out2(decoder_1_out2), .sel(register_1_q[7:4]));  // open: out0, out3, out4, out5, out6, out7, out8, out9, out10, out11, out12, out13, out14, out15, en
  Decoder #(.select(4)) decoder_2 (
    .out2(decoder_2_out2), .sel(register_1_q[3:0]));  // open: out0, out1, out3, out4, out5, out6, out7, out8, out9, out10, out11, out12, out13, out14, out15, en
  ALU_8bit alu_8bit_1 ();  // open: Enable, Latch, A0, A1, A2, A3, A4, A5, A6, A7, B0, B1, B2, B3, B4, B5, B6, B7, Reset, OPcode, Cin, ZF, CF, OFlag, SF, C0, C1, C2, C3, C4, C5, C6, C7
  // AND_Gate and_1 has open pins: in0=decoder_2_out2, in1=decoder_1_out1, out=open
  // AND_Gate and_2 has open pins: in0=decoder_2_out2, in1=decoder_1_out2, out=open
endmodule
